// Logisim project 1.circ as structural Verilog: 1 circuit, main circuit main
module main (
  input  x,
  input  y,
  input  z,
  output out_4
);

  wire and_1_out, and_2_out, and_3_out;

  and and_1 (and_1_out, x, z);
  and and_2 (and_2_out, y, z);
  and and_3 (and_3_out, x, y);
  or or_1 (out_4, and_1_out, and_2_out, and_3_out);
endmodule
