// Logisim project 2.circ as structural Verilog: 1 circuit, main circuit main
module main (
  input  [3:0] in_1,
  output out_2
);

  Multiplexer #(.select(4), .enable("false")) multiplexer_1 (
    .in0(1'b1), .in1(1'b0), .in2(1'b0), .in3(1'b1), .in4(1'b1), .in5(1'b0), .in6(1'b1), .in7(1'b0),
    .in8(1'b0), .in9(1'b1), .in10(1'b0), .in11(1'b0), .in12(1'b1), .in13(1'b1), .in14(1'b0), .in15(1'b0),
    .out(out_2), .sel(in_1));
endmodule
