// Logisim project 3.1.circ as structural Verilog: 1 circuit, main circuit main
module main (
  input  [2:0] in_1,
  input  [2:0] in_2,
  output [2:0] out_3
);

  wire adder_1_cout, adder_2_cout;

  Adder #(.width(1)) adder_1 (.a(in_1[0]), .b(in_2[0]), .out(out_3[0]), .cout(adder_1_cout));  // open: cin
  Adder #(.width(1)) adder_2 (.a(in_1[1]), .b(in_2[1]), .out(out_3[1]), .cin(adder_1_cout), .cout(adder_2_cout));
  Adder #(.width(1)) adder_3 (.a(in_1[2]), .b(in_2[2]), .out(out_3[2]), .cin(adder_2_cout));  // open: cout
endmodule
