// Logisim project 3.circ as structural Verilog: 1 circuit, main circuit main
module main (
  input  [2:0] in_1,
  input  [2:0] in_2,
  input  in_3,
  output [2:0] out_4,
  output out_5
);

  wire and_1_out, and_2_out, and_3_out, and_4_out, and_5_out, and_6_out, xor_1_out, xor_3_out, xor_4_out,
       xor_6_out, xor_7_out;

  xor xor_1 (xor_1_out, in_2[0], in_1[0]);
  xor xor_2 (out_4[0], in_3, xor_1_out);
  and and_1 (and_1_out, xor_1_out, in_3);
  and and_2 (and_2_out, in_2[0], in_1[0]);
  xor xor_3 (xor_3_out, and_1_out, and_2_out);
  xor xor_4 (xor_4_out, in_2[1], in_1[1]);
  xor xor_5 (out_4[1], xor_3_out, xor_4_out);
  and and_3 (and_3_out, xor_3_out, xor_4_out);
  and and_4 (and_4_out, in_2[1], in_1[1]);
  xor xor_6 (xor_6_out, and_3_out, and_4_out);
  xor xor_7 (xor_7_out, in_2[2], in_1[2]);
  xor xor_8 (out_4[2], xor_6_out, xor_7_out);
  and and_5 (and_5_out, xor_6_out, xor_7_out);
  and and_6 (and_6_out, in_2[2], in_1[2]);
  xor xor_9 (out_5, and_5_out, and_6_out);
endmodule
