// Logisim project 5.circ as structural Verilog: 1 circuit, main circuit main
module main (
  input  [2:0] in_1,
  input  in_2,
  input  in_3,
  input  in_4,
  output out_5,
  output out_6
);

  wire and_1_out, and_2_out, and_3_out, and_4_out, and_5_out, and_6_out, and_7_out, decoder_1_out0,
       decoder_1_out1, decoder_1_out2, decoder_1_out3, decoder_1_out4, not_1_out, not_2_out, or_1_out,
       or_2_out, xor_1_out, xor_2_out;

  Decoder #(.select(3), .enable("false")) decoder_1 (
    .out0(decoder_1_out0), .out1(decoder_1_out1), .out2(decoder_1_out2), .out3(decoder_1_out3),
    .out4(decoder_1_out4), .sel(in_1));  // open: out5, out6, out7
  not not_1 (not_1_out, in_2);
  not not_2 (not_2_out, in_3);
  xor xor_1 (xor_1_out, in_3, in_2);
  and and_1 (and_1_out, in_3, in_2);
  or or_1 (or_1_out, in_2, in_3);
  and and_2 (and_2_out, xor_1_out, in_4);
  xor xor_2 (xor_2_out, xor_1_out, in_4);
  or or_2 (or_2_out, and_2_out, and_1_out);
  and and_3 (and_3_out, decoder_1_out0, in_2, in_3);
  and and_4 (and_4_out, decoder_1_out1, or_1_out);
  and and_5 (and_5_out, decoder_1_out2, not_1_out);
  and and_6 (and_6_out, decoder_1_out3, not_2_out);
  and and_7 (and_7_out, decoder_1_out4, xor_2_out);
  and and_8 (out_6, decoder_1_out4, or_2_out);
  or or_3 (out_5, and_3_out, and_4_out, and_5_out, and_6_out, and_7_out);

  // Notes on the sheet:
  //   000 – и 001 – или 010 – не A 011 – не B 100 – сумма  
endmodule
